# Fritzing sketch Circuit_Layout (saved by Fritzing 0.9.3b)

parts:
  Part1 = Arduino Ethernet Shield (Rev3)
  Part2 = Arduino Uno (Rev3) - ICSP  # not connected
  Part3 = InvenSense MPU6050
  M2 = ESC
  920KV_Motor2 = DJI 920 KV Motor
  U2 = LIPO-1000mAh [package=lipo-1000]  # not connected
  LED3 = smd LED [color="Blue (470nm)" package="0603 [SMD]"]
  JACK2 = 2.1mm Barrel Jack with Terminal Block  # not connected

nets:
  N1: Part1.A0, LED3.anode
  N2: Part1.A4/SDA, Part3.SDA
  N3: Part1.A5/SCL, Part3.SCL
  N4: Part1.PWM_D6, M2.DATA
  5V: Part1.5V, Part3.VCC
  GND: Part1.GND, Part3.GND, LED3.cathode
  N5: M2.U, 920KV_Motor2.u
  N6: M2.V, 920KV_Motor2.v
  N7: M2.W, 920KV_Motor2.w

notes:
  + and - are INTENTIONALLY left disconnected. ----->
  Arduino UNO w/ ethernet shield. (Uses pins 10, 11, 12, and 13
  3S Lipo Battery

custom parts:
  DJI 920 KV Motor: DJI Brushless Outrunner 2212/920K Motor F330-550

// code stored in the sketch: MecE668.ino

